# Fritzing sketch sketch_esp_communication (saved by Fritzing 0.9.3b)
breadboards: 1

parts:
  Part1 = Arduino Uno (Rev3)
  U1 = ESP8266 WiFi Module [part_number=ESP8266]
  R2 = Resistor [tolerance=±5% resistance=1k package=THT]
  R3 = Resistor [tolerance=±5% resistance=1k package=THT]
  R4 = Resistor [tolerance=±5% resistance=1k package=THT]
  R5 = Resistor [tolerance=±5% resistance=10k package=THT]
  R9 = Resistor [tolerance=±5% resistance=10k package=THT]
  S1 = Pushbutton [package="[THT]"]
  J2 = female pin header, 1 pin [form="♀ (female)"]

nets:
  N1: Part1.D0/RX, R4.Pin_0
  N2: Part1.D1/TX, U1.TXD
  GND: Part1.RESET, Part1.GND, U1.GND, R2.Pin_1, S1.Pin_1, S1.Pin_2
  N3: U1.RXD, R3.Pin_0, R4.Pin_1
  N4: U1.VCC, R5.Pin_1, R9.Pin_1, J2.pin1
  N5: U1.RST, R9.Pin_0, S1.Pin_3, S1.Pin_4
  N6: U1.CH_PD, R5.Pin_0
  N7: R2.Pin_0, R3.Pin_1

notes:
  External 3.3v

custom parts:
  ESP8266 WiFi Module: Generic WiFi Module based on the ESP8266 with onboard PCB antenna and UART communications
