# Fritzing sketch sketch_station (saved by Fritzing 0.9.3b)
breadboards: 1

parts:
  Part1 = Arduino Uno (Rev3)
  Part2 = Barometric Pressure Sensor - BMP180 Breakout (GY-68)
  DHT22_module = Humidity and Temperature Sensor RHT03
  U1 = ESP8266 WiFi Module [part_number=ESP8266]
  R2 = Resistor [tolerance=±5% resistance=1k package=THT]
  R3 = Resistor [tolerance=±5% resistance=1k package=THT]
  R4 = Resistor [tolerance=±5% resistance=1k package=THT]
  R5 = Resistor [tolerance=±5% resistance=10k package=THT]
  R9 = Resistor [tolerance=±5% resistance=10k package=THT]
  S1 = Pushbutton [package="[THT]"]
  J1 = female pin header, 1 pin [form="♀ (female)"]
  R10 = Resistor [tolerance=±5% resistance=10k package=THT]
  J2 = female pin header, 1 pin [form="♀ (female)"]

nets:
  N1: Part1.A4/SDA, Part2.SDA
  N2: Part1.A5/SCL, Part2.SCL
  N3: Part1.D2, U1.TXD
  N4: Part1.D3_PWM, R4.Pin_0
  N5: Part1.D4, DHT22_module.Data-signal, R10.Pin_1
  3V3: Part1.3V3, Part2.VCC
  5V: Part1.5V, DHT22_module.Vcc, R10.Pin_0
  GND: Part1.GND, Part2.GND, DHT22_module.GND_2, U1.GND, R2.Pin_1, S1.Pin_1, S1.Pin_2
  N6: U1.RXD, R3.Pin_0, R4.Pin_1
  N7: U1.VCC, R5.Pin_1, R9.Pin_1, J2.pin1
  N8: U1.GPIO_0, J1.pin1
  N9: U1.RST, R9.Pin_0, S1.Pin_3, S1.Pin_4
  N10: U1.CH_PD, R5.Pin_0
  N11: R2.Pin_0, R3.Pin_1

notes:
  External 3.3v
  For switching to
  Programming Mode

custom parts:
  ESP8266 WiFi Module: Generic WiFi Module based on the ESP8266 with onboard PCB antenna and UART communications
